# Fritzing sketch mia_circuit (saved by Fritzing 0.9.3b)

parts:
  Part1 = Arduino Mega ADK (Rev3)
  J1 = Basic Servo
  J2 = Basic Servo
  J3 = Basic Servo
  J4 = Basic Servo
  J5 = Basic Servo
  J7 = Basic Servo
  J8 = Basic Servo
  J9 = Basic Servo
  J10 = Basic Servo
  J11 = Basic Servo
  J12 = Basic Servo
  J13 = Basic Servo
  J15 = Basic Servo  # not connected
  U1 = Luxeon LED [package=luxeon]  # not connected

nets:
  N1: Part1.D12_PWM, J1.pulse
  N2: Part1.D11_PWM, J2.pulse
  N3: Part1.D10_PWM, J7.pulse
  N4: Part1.D9_PWM, J8.pulse
  N5: Part1.D8_PWM, J3.pulse
  N6: Part1.D2_PWM, J9.pulse
  N7: Part1.D3_PWM, J10.pulse
  N8: Part1.D4_PWM, J11.pulse
  N9: Part1.D5_PWM, J12.pulse
  N10: Part1.D6_PWM, J13.pulse
  N11: Part1.D31, J4.pulse
  N12: Part1.D33, J5.pulse

notes:
  laser diode
  Waist Servo
  Right Side
  Left Side
  Head Servos
  Power Source 7.4v DC
